# Fritzing sketch ecoluz (saved by Fritzing 0.9.3b)
breadboards: 1

parts:
  U1 = ESP8266 WiFi Module [part_number=ESP8266]
  IR3 = vs1838b [package=THT]
  J1 = Piezo Speaker
  RGB_SMD_LED1 = SMD RGB LED (WS2812) [package=5050]
  KY-1 = Keyes Relay [package=THT]
  5v = Power plug
  LM1117_(3_3v) = Voltage Regulator - 5V [package="TO220 [THT]"]

nets:
  N1: U1.RXD, IR3.Data
  N2: U1.VCC, LM1117_(3_3v).output_voltage
  N3: U1.GPIO_0, KY-1.signal
  N4: U1.GPIO_2, J1.pin2
  GND: U1.GND, IR3.GND, J1.pin1, RGB_SMD_LED1.VSS, KY-1.ground, 5v.GND, LM1117_(3_3v).GND
  N5: U1.TXD, RGB_SMD_LED1.DIn
  VCC: IR3.Vs, RGB_SMD_LED1.VCC, KY-1.power, 5v.VCC, LM1117_(3_3v).input_voltage

custom parts:
  ESP8266 WiFi Module: Generic WiFi Module based on the ESP8266 with onboard PCB antenna and UART communications
  Keyes Relay: The Keyes 5V relay module is suitable for SCM development, home appliance control. It uses a 5V~12V TIL control signal which can control DC / AC signal.
